# Fritzing sketch Alohomora-3FA_Schematic_Fritzing (saved by Fritzing 0.9.3b)
perfboards: 3

parts:
  Componente1 = Arduino Nano (Rev3.0) (ICSP)
  Componente2 = RFID-RC522-v2
  J1 = Basic Servo
  R1 = Resistor [tolerance=±5% resistance=330 package=THT]
  LED1 = LED - 5mm [color="Red (633nm)" package="5 mm [THT]"]
  J2 = Piezo Speaker
  KEYPAD1 = Membrane Matrix Keypad  # not connected
  U1 = NodeMCU V3.0
  J6 = Screw terminal - 2 pins [package=THT]
  J7 = Screw terminal - 2 pins [package=THT]
  F1 = FUSE [package=fuse_5mm]
  JP1 = Header 1 [package=1x01_offset]
  JP2 = Header 1 [package=1x01_offset]
  JP3 = Header 1 [package=1x01_offset]  # not connected
  JP4 = Header 1 [package=1x01_offset]
  D3 = Rectifier Diode [part_number=1N4007 package="300 mil [THT]"]
  D4 = Rectifier Diode [part_number=1N4001 package="300 mil [THT]"]
  J8 = screw terminal, 6 pins
  J9 = screw terminal, 6 pins
  C1 = Electrolytic Capacitor [capacitance=1µF package="100 mil [THT, electrolytic]"]
  JP5 = Header 1 [package=1x01_offset]
  JP10 = Header 1 [package=1x01_offset]
  R2 = Resistor [tolerance=±5% resistance=33 package=THT]
  LED2 = LED - 5mm [color="Red (633nm)" package="5 mm [THT]"]
  J11 = Screw terminal - 2 pins [package=THT]
  J12 = Screw terminal - 2 pins [package=THT]
  F2 = FUSE [package=fuse_5mm]
  JP11 = Header 1 [package=1x01_offset]
  JP12 = Header 1 [package=1x01_offset]
  JP13 = Header 1 [package=1x01_offset]
  JP14 = Header 1 [package=1x01_offset]  # not connected
  JP15 = Header 1 [package=1x01_offset]
  JP16 = Header 1 [package=1x01_offset]
  D5 = Rectifier Diode [part_number=1N4007 package="300 mil [THT]"]
  D6 = Rectifier Diode [part_number=1N4001 package="300 mil [THT]"]
  J13 = screw terminal, 6 pins
  J14 = screw terminal, 6 pins
  C2 = Electrolytic Capacitor [capacitance=1µF package="100 mil [THT, electrolytic]"]
  U6 = V_REG_LD1117VXX [package=78xxl]
  C3 = Electrolytic Capacitor [capacitance=10µF voltage=16V package="100 mil [THT, electrolytic]"]
  C4 = Electrolytic Capacitor [capacitance=22µF package="100 mil [THT, electrolytic]"]
  C5 = Ceramic Capacitor [capacitance=100nF package="100 mil [THT, multilayer]"]
  VCC1 = 4 x AAA Battery Mount
  VCC2 = 4 x AAA Battery Mount
  U8 = 941H-2C-5D [package=relay-5v]
  U9 = 941H-2C-5D [package=relay-5v]
  Reg1 = DC-DC CONVERTER [part_number=80633 package=dc-dc_converter]
  J16 = screw terminal, 4 pins
  J17 = screw terminal, 6 pins
  J15 = screw terminal, 6 pins
  J18 = screw terminal, 4 pins
  LED3 = LED - 5mm [color="Green (570nm)" package="5 mm [THT]"]
  LED4 = LED - 5mm [color="Red (633nm)" package="5 mm [THT]"]
  R3 = Resistor [tolerance=±5% resistance=220 package=THT]
  R4 = Resistor [tolerance=±5% resistance=220 package=THT]

nets:
  N1: Componente1.GND, J2.pin1, J17.pin3
  N2: Componente1.D2, J2.pin2
  N3: Componente1.D3, J1.pulse
  N4: Componente1.D5, R4.Pin_1
  N5: Componente1.D6, R3.Pin_1
  N6: Componente1.D9, Componente2.RST
  N7: Componente1.D10, Componente2.SDA
  N8: Componente1.D11/MOSI, Componente2.MOSI
  N9: Componente1.D12/MISO, Componente2.MISO
  N10: Componente1.VIN, J15.pin3
  N11: Componente1.D13/SCK, Componente2.SCK
  N12: Componente2.GND, J16.pin3
  N13: Componente2.3.3V, J18.pin3
  N14: J1.gnd, J17.pin2
  N15: J1.vcc, J15.pin2
  N16: R1.Pin_0, JP1.1, J9.pin1, J9.pin6, C1.+, U8.9
  N17: R1.Pin_1, LED1.anode
  N18: LED1.cathode, J8.pin6, C1.-, JP5.1, U8.8
  VIN: U1.Vin, U1.GND, J16.pin2, J18.pin2
  N19: J6.pin1, J7.pin2, VCC1.+
  N20: J6.pin2, F1.1, JP4.1
  N21: J7.pin1, JP2.1, D3.anode, VCC2.-, U8.1, U8.4, U8.6
  N22: F1.2, D4.anode
  N23: D3.cathode, D4.cathode, JP10.1, U8.11, U8.13, U8.16
  N24: J8.pin1, J8.pin2
  N25: J9.pin4, Reg1.IN+
  N26: R2.Pin_0, JP11.1, J14.pin1, J14.pin6, C2.+, U9.9
  N27: R2.Pin_1, LED2.anode
  N28: LED2.cathode, JP15.1, J13.pin6, C2.-, U9.8
  N29: J11.pin1, JP16.1, D5.anode, U9.1, U9.4, U9.6
  N30: J11.pin2, J12.pin1
  N31: J12.pin2, F2.1, JP12.1
  N32: F2.2, D6.anode
  N33: JP13.1, D5.cathode, D6.cathode, U9.11, U9.13, U9.16
  N34: J13.pin1, J13.pin2
  N35: U6.GND, C3.+, J15.pin6
  N36: C4.+, C5.0, J18.pin1
  N37: VCC1.-, VCC2.+
  N38: Reg1.OUT-, J17.pin1
  N39: Reg1.OUT+, J15.pin1
  N40: J16.pin1, J17.pin6
  N41: LED3.cathode, LED4.cathode
  N42: LED3.anode, R4.Pin_0
  N43: LED4.anode, R3.Pin_0

notes:
  +
  -
  INPUT 12 volt
  12 Volt - Voltage divider
  Switch
  On-Off
  OUT +12V
  OUT - ground
  By-Pass
  Step-down 12V to 5V
  3.3 Volt - Voltage divider
  OUT +3.3V
  INPUT 3.3 volt
  LM1117-3,3
  5 to 3,3 Volt - step down
  12 Volt
  5 Volt
  3,3 Volt

custom parts:
  RFID-RC522-v2: A simple China made RFID-RC522 Reader; do check the pin labels, as this is a MFRC522 based clone.
  Membrane Matrix Keypad: Membrane Matrix 3x4 Keypad
  NodeMCU V3.0: ESP8266 based NodeMCU
  941H-2C-5D: DPDT Relay - 2 Form C
  DC-DC CONVERTER: WYHP 5A constant current/voltage manufactured by Shenzhen Weiyapuhua Technology Co., Ltd
